# Fritzing sketch Keypad (saved by Fritzing 0.9.5d)
breadboards: 1

parts:
  Mod1 = Raspberry Pi Pico W
  Matrix_keypad1 = KEYPAD 4x4

nets:
  N1: Mod1.pin_3, Mod1.pin_8, Mod1.pin_13, Mod1.pin_18, Mod1.pin_23, Mod1.pin_28, Mod1.pin_33, Mod1.pin_38
  N2: Mod1.pin_4, Matrix_keypad1.row4
  N3: Mod1.pin_5, Matrix_keypad1.row3
  N4: Mod1.pin_6, Matrix_keypad1.row2
  N5: Mod1.pin_7, Matrix_keypad1.row1
  N6: Mod1.pin_9, Matrix_keypad1.col4
  N7: Mod1.pin_10, Matrix_keypad1.col3
  N8: Mod1.pin_11, Matrix_keypad1.col2
  N9: Mod1.pin_12, Matrix_keypad1.col1

custom parts:
  Raspberry Pi Pico W: Raspberry Pi Pico W. Based around the RP2040 microcontroller the Pico W is a low cost microcontroller device bringing Raspberry Pi quality, cost, and easy of use to the microcontroller space. The areas marked KEEPOUT in pcb silkscreen should not have traces running through them to avoid shorts on a soldered in module!
  KEYPAD 4x4: Matrix keypad 16 buttons, 4 rows x 4 columns
