# Fritzing sketch LCD (saved by Fritzing 0.9.5d)
breadboards: 1

parts:
  Mod1 = Raspberry Pi Pico W
  LCD1 = LCD screen
  LCM1602_IIC1 = LCM1602 IIC [part_number="LCM1602 IIC" chip_label="LCM1602 IIC" package="DIP (Dual Inline) [THT]"]

nets:
  N1: Mod1.pin_3, Mod1.pin_8, Mod1.pin_13, Mod1.pin_18, Mod1.pin_23, Mod1.pin_28, Mod1.pin_33, Mod1.pin_38, Mod1.pin_42, LCM1602_IIC1.GND
  N2: Mod1.pin_26, LCM1602_IIC1.SDA
  N3: Mod1.pin_27, LCM1602_IIC1.SCL
  N4: Mod1.pin_40, LCM1602_IIC1.VCC
  VSS: LCD1.VSS, LCM1602_IIC1.VSS
  VDD: LCD1.VDD, LCM1602_IIC1.VDD
  N5: LCD1.V0, LCM1602_IIC1.V0
  N6: LCD1.RS, LCM1602_IIC1.RS
  N7: LCD1.R/W, LCM1602_IIC1.RW
  N8: LCD1.E, LCM1602_IIC1.E
  N9: LCD1.DB0, LCM1602_IIC1.D0
  N10: LCD1.DB1, LCM1602_IIC1.D1
  N11: LCD1.DB2, LCM1602_IIC1.D2
  N12: LCD1.DB3, LCM1602_IIC1.D3
  N13: LCD1.DB4, LCM1602_IIC1.D4
  N14: LCD1.DB5, LCM1602_IIC1.D5
  N15: LCD1.DB6, LCM1602_IIC1.D6
  N16: LCD1.DB7, LCM1602_IIC1.D7
  N17: LCD1.LED+, LCM1602_IIC1.A
  N18: LCD1.LED-, LCM1602_IIC1.K

custom parts:
  Raspberry Pi Pico W: Raspberry Pi Pico W. Based around the RP2040 microcontroller the Pico W is a low cost microcontroller device bringing Raspberry Pi quality, cost, and easy of use to the microcontroller space. The areas marked KEEPOUT in pcb silkscreen should not have traces running through them to avoid shorts on a soldered in module!
  LCM1602 IIC: I2C-Module to use a 1602 or 2004 LCD on with the wire.h libory Serial LCD Modul
