# Fritzing sketch PasswordKeypad (saved by Fritzing 0.9.5d)
breadboards: 1

parts:
  Mod2 = Raspberry Pi Pico W
  Matrix_keypad2 = KEYPAD 4x4
  LCD1 = LCD screen  # not connected
  LCM1602_IIC1 = LCM1602 IIC [part_number="LCM1602 IIC" chip_label="LCM1602 IIC" package="DIP (Dual Inline) [THT]"]
  R1 = Resistor [tolerance=±5% resistance=220 package=THT]
  LED2 = LED - 3mm [color="Red (633nm)" package="3 mm [THT]"]
  LED3 = LED - 3mm [color="Red (633nm)" package="3 mm [THT]"]
  R2 = Resistor [tolerance=±5% resistance=220 package=THT]

nets:
  N1: Mod2.pin_3, Mod2.pin_8, Mod2.pin_13, Mod2.pin_18, Mod2.pin_23, Mod2.pin_28, Mod2.pin_33, Mod2.pin_38, Mod2.pin_42, Matrix_keypad2.col4, Matrix_keypad2.row4, LCM1602_IIC1.GND
  N2: Mod2.pin_4, Matrix_keypad2.row3
  N3: Mod2.pin_5, Matrix_keypad2.row2
  N4: Mod2.pin_6, Matrix_keypad2.row1
  N5: Mod2.pin_7, LED2.cathode, LED3.cathode
  N6: Mod2.pin_9, Matrix_keypad2.col3
  N7: Mod2.pin_10, Matrix_keypad2.col2
  N8: Mod2.pin_11, Matrix_keypad2.col1
  N9: Mod2.pin_19, R1.Pin_1, R2.Pin_1
  N10: Mod2.pin_26, LCM1602_IIC1.SDA
  N11: Mod2.pin_27, LCM1602_IIC1.SCL
  N12: Mod2.pin_40, LCM1602_IIC1.VCC
  N13: R1.Pin_0, LED2.anode
  N14: LED3.anode, R2.Pin_0

custom parts:
  Raspberry Pi Pico W: Raspberry Pi Pico W. Based around the RP2040 microcontroller the Pico W is a low cost microcontroller device bringing Raspberry Pi quality, cost, and easy of use to the microcontroller space. The areas marked KEEPOUT in pcb silkscreen should not have traces running through them to avoid shorts on a soldered in module!
  KEYPAD 4x4: Matrix keypad 16 buttons, 4 rows x 4 columns
  LCM1602 IIC: I2C-Module to use a 1602 or 2004 LCD on with the wire.h libory Serial LCD Modul
