# Fritzing sketch SensorDistance (saved by Fritzing 0.9.5d)
breadboards: 1

parts:
  Mod3 = Raspberry Pi Pico W
  HC-SR04_Sensor_1 = HC-SR04 Ultrasonic Distance Sensor

nets:
  N1: Mod3.pin_3, Mod3.pin_8, Mod3.pin_13, Mod3.pin_18, Mod3.pin_23, Mod3.pin_28, Mod3.pin_33, Mod3.pin_38
  N2: Mod3.pin_20, HC-SR04_Sensor_1.ECHO
  N3: Mod3.pin_21, HC-SR04_Sensor_1.TRIG
  N4: Mod3.pin_39, HC-SR04_Sensor_1.GND

custom parts:
  Raspberry Pi Pico W: Raspberry Pi Pico W. Based around the RP2040 microcontroller the Pico W is a low cost microcontroller device bringing Raspberry Pi quality, cost, and easy of use to the microcontroller space. The areas marked KEEPOUT in pcb silkscreen should not have traces running through them to avoid shorts on a soldered in module!
